# Fritzing sketch button_input (saved by Fritzing 0.8.7b)
breadboards: 1

parts:
  Pi1 = Adafruit Pi Cobbler
  ENCODER1 = Rotary Encoder with Knob

nets:
  N1: Pi1.3V3, ENCODER1.no_name_yet#4
  N2: Pi1.#23, ENCODER1.no_name_yet#5

custom parts:
  Adafruit Pi Cobbler: Adafruit Pi Cobbler GPIO Breakout for Raspberry Pi
  Rotary Encoder with Knob: Rotary Encoder with 1/4" Shaft and Knob
