# Fritzing sketch tricolor (saved by Fritzing 0.8.7b)
breadboards: 1

parts:
  Pi1 = Adafruit Pi Cobbler
  LED1 = RGB LED (com. anode, rbg) [package="5 mm [THT]"]
  R1 = Resistor [tolerance=±5% resistance=330 package="0603 [SMD]"]
  R2 = Resistor [tolerance=±5% resistance=330 package="0603 [SMD]"]
  R3 = Resistor [tolerance=±5% resistance=330 package="0603 [SMD]"]

nets:
  N1: Pi1.GND, LED1.common_anode
  N2: Pi1.#17, R1.Pin_0
  N3: Pi1.#21, R2.Pin_0
  N4: Pi1.#22, R3.Pin_0
  N5: LED1.red_cathode, R3.Pin_1
  N6: LED1.blue_cathode, R2.Pin_1
  N7: LED1.green_cathode, R1.Pin_1

custom parts:
  Adafruit Pi Cobbler: Adafruit Pi Cobbler GPIO Breakout for Raspberry Pi
