# Fritzing sketch ADC8591 DAC LED (saved by Fritzing 0.8.7b)
breadboards: 1

parts:
  IC1 = IC, DIP package, 16 pins [chip_label=PCF8591P]
  D1 = Rectifier Diode [part_number=1N4001 package="Melf DO-213 AB [SMD]"]
  R1 = Resistor [tolerance=±5% resistance=1k package=THT]
  C1 = Electrolytic Capacitor [capacitance=47µF package="100 mil [THT, electrolytic]"]
  C2 = Electrolytic Capacitor [capacitance=47µF package="100 mil [THT, electrolytic]"]
  R2 = Trimmer Potentiometer [maximum_resistance=10kΩ package=THT]
  Pi1 = Adafruit Pi Cobbler
  Q1 = NPN-Transistor [part_number=2N2222 package="TO92 [THT]"]
  R3 = Resistor [tolerance=±5% resistance=270 package=THT]
  LED1 = LED - 5mm [color="Red (633nm)" package="5 mm [THT]"]

nets (from the schematic view):
  N1: IC1.pin1, R2.wiper
  N2: IC1.pin6, IC1.pin16, D1.cathode, R1.Pin_0, C2.+, R2.leg1
  N3: IC1.pin8, IC1.pin12, IC1.pin13, C1.-, C2.-, R2.leg2, Pi1.GND, LED1.cathode
  N4: IC1.pin9, Pi1.SDA0
  N5: IC1.pin10, Pi1.SCL0
  N6: IC1.pin14, R1.Pin_1, C1.+
  Vout: IC1.pin15, Q1.B
  N7: D1.anode, Pi1.5V0, Q1.C
  Buff: Q1.E, R3.Pin_0
  N8: R3.Pin_1, LED1.anode

custom parts:
  Adafruit Pi Cobbler: Adafruit Pi Cobbler GPIO Breakout for Raspberry Pi
