# Fritzing sketch CheerLights_Selector_AtHome_Solution (saved by Fritzing 0.8.7b)
breadboards: 1

parts:
  Pi2 = Adafruit Pi Cobbler
  ENCODER2 = Rotary Encoder with Knob
  LED2 = RGB LED (com. anode, rbg) [package="5 mm [THT]"]
  R4 = Resistor [tolerance=±5% resistance=330 package="0603 [SMD]"]
  R5 = Resistor [tolerance=±5% resistance=330 package="0603 [SMD]"]
  R6 = Resistor [tolerance=±5% resistance=330 package="0603 [SMD]"]

nets:
  N1: Pi2.3V3, ENCODER2.no_name_yet#2, ENCODER2.no_name_yet#4
  N2: Pi2.GND, LED2.common_anode
  N3: Pi2.#17, R6.Pin_0
  N4: Pi2.#21, R5.Pin_0
  N5: Pi2.#22, R4.Pin_0
  N6: Pi2.#23, ENCODER2.no_name_yet#5
  N7: Pi2.#24, ENCODER2.no_name_yet#3
  N8: Pi2.#25, ENCODER2.no_name_yet#1
  N9: LED2.red_cathode, R4.Pin_1
  N10: LED2.blue_cathode, R5.Pin_1
  N11: LED2.green_cathode, R6.Pin_1

custom parts:
  Adafruit Pi Cobbler: Adafruit Pi Cobbler GPIO Breakout for Raspberry Pi
  Rotary Encoder with Knob: Rotary Encoder with 1/4" Shaft and Knob
