# Fritzing sketch rotary_encoder (saved by Fritzing 0.8.7b)
breadboards: 1

parts:
  Pi1 = Adafruit Pi Cobbler
  ENCODER1 = Rotary Encoder with Knob

nets:
  N1: Pi1.3V3, ENCODER1.no_name_yet#2
  N2: Pi1.GND, ENCODER1.no_name_yet#4
  N3: Pi1.#23, ENCODER1.no_name_yet#5
  N4: Pi1.#24, ENCODER1.no_name_yet#3
  N5: Pi1.#25, ENCODER1.no_name_yet#1

custom parts:
  Adafruit Pi Cobbler: Adafruit Pi Cobbler GPIO Breakout for Raspberry Pi
  Rotary Encoder with Knob: Rotary Encoder with 1/4" Shaft and Knob
