# Fritzing sketch rotary_encoder_test (saved by Fritzing 0.8.7b)
breadboards: 1

parts:
  Pi1 = Adafruit Pi Cobbler
  ENCODER1 = Rotary Encoder with Knob
  R1 = Resistor [tolerance=±5% resistance=270 package=THT]
  R2 = Resistor [tolerance=±5% resistance=270 package=THT]
  LED1 = LED - 5mm [color="Red (633nm)" package="5 mm [THT]"]
  LED2 = LED - 5mm [color="Red (633nm)" package="5 mm [THT]"]

nets:
  N1: Pi1.3V3, ENCODER1.no_name_yet#2
  N2: Pi1.GND, LED1.cathode, LED2.cathode
  N3: ENCODER1.no_name_yet#1, R1.Pin_1
  N4: ENCODER1.no_name_yet#3, R2.Pin_0
  N5: R1.Pin_0, LED1.anode
  N6: R2.Pin_1, LED2.anode

custom parts:
  Adafruit Pi Cobbler: Adafruit Pi Cobbler GPIO Breakout for Raspberry Pi
  Rotary Encoder with Knob: Rotary Encoder with 1/4" Shaft and Knob
